# Fritzing sketch PetFeederDiagram (saved by Fritzing 0.9.6b)
breadboards: 1

parts:
  S1 = Pushbutton [package="[SMD]"]
  LED1 = smd LED [color="Red (633nm)" package="0603 [SMD]"]
  R1 = Resistor [tolerance=±5% power=0.25 resistance=220 package=THT]
  M1 = DC Motor
  A1 = Raspberry Pi 5
  U2 = TRANSCHIPTC5747 [package=camera_sfv24r-2st_2]  # not connected
  KY-1 = Keyes Relay [package=THT]
  Part4 = Lilypad Battery Connect
  Part5 = Adafruit T-Cobbler Plus [part_number="Adafruit #1989 and #2028"]
  R2 = Resistor [tolerance=±5% resistance=220 package="0402 [SMD]"]

nets:
  N1: S1.Pin_1, S1.Pin_2, KY-1.power
  N2: S1.Pin_3, S1.Pin_4, R2.Pin_1
  N3: LED1.cathode, R1.Pin_0
  N4: LED1.anode, A1.GND, A1.Fan-GND, Part5.RXD, Part5.CE1, Part5.GPIO21
  N5: M1.pin_1, Part4.-
  N6: M1.pin_2, KY-1.NO
  3V3: A1.3V3, A1.GPIO2, Part5.+5V, Part5.GPIO24
  N7: A1.GPIO3, A1.GPIO27, A1.GPIO10, A1.GPIO5, A1.GPIO13, Part5.GND
  N8: A1.GPIO4, Part5.TXD
  N9: A1.GPIO17, Part5.GPIO18
  N10: A1.GPIO22, Part5.GPIO23
  N11: A1.GPIO9, Part5.GPIO25
  N12: A1.GPIO11, Part5.CE0
  N13: A1.ID_SD, Part5.EECLK
  N14: A1.GPIO6, Part5.GPIO12
  N15: A1.GPIO19, Part5.GPIO16
  N16: A1.GPIO26, Part5.GPIO20
  N17: KY-1.signal, Part5.GPIO17
  N18: KY-1.C, Part4.+
  N19: Part5.GPIO6, R2.Pin_0

notes:
  Relay
  Pi Camera
  Raspberry Pi 5
  Power Outlet (Plug)
  AC Motor
  Breadboard (Standard)
  T-Cobbler
  3D Printed
  Food Dispenser

custom parts:
  Raspberry Pi 5: The RPi5, a faster version of the awesome Raspberry Pi4B ARM Board with 40 pin gpio.
  Keyes Relay: The Keyes 5V relay module is suitable for SCM development, home appliance control. It uses a 5V~12V TIL control signal which can control DC / AC signal.
  Adafruit T-Cobbler Plus: The Raspberry Pi has landed on the Maker World like a 40-GPIO pinned, quad-USB ported, credit card sized bomb of DIY joy. And while you can use most of our great Model B accessories by hooking up our downgrade cable, its probably a good time to upgrade your set up and accessorize using all of the 40 pins. That's why we now carry the Assembled Adafruit Pi T-Cobbler Plus - Breakout + Cable for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
